# Fritzing sketch Demo.fzpz (saved by Fritzing 0.9.6b)
breadboards: 1
perfboards: 1

parts:
  A1 = Raspberry Pi 5
  LED2 = smd LED [color="Green (570nm)" package="0805 [SMD]"]
  MX_SOCKET1 = Kailh switch socket
  LED3 = smd LED [color="Red (635nm)" package="0805 [SMD]"]
  LED4 = smd LED [color="Yellow (595nm)" package="0805 [SMD]"]
  LED5 = smd LED [color="Blue (525nm)" package="0805 [SMD]"]
  R1 = Resistor [tolerance=±5% resistance=220 package="2010 [SMD]"]
  R2 = Resistor [tolerance=±5% resistance=220 package="2010 [SMD]"]
  R3 = Resistor [tolerance=±5% resistance=220 package="2010 [SMD]"]
  R4 = Resistor [tolerance=±5% resistance=220 package="2010 [SMD]"]
  MX_SOCKET3 = Kailh switch socket
  MX_SOCKET4 = Kailh switch socket
  MX_SOCKET5 = Kailh switch socket
  A2 = Raspberry Pi 5  # not connected

nets:
  N1: A1.5V, MX_SOCKET1.pin1, MX_SOCKET3.pin1, MX_SOCKET4.pin1, MX_SOCKET5.pin1, MX_SOCKET5.pin2
  N2: A1.GND, R1.Pin_1, R2.Pin_1, MX_SOCKET4.pin2
  N3: A1.GPIO14, MX_SOCKET3.pin2
  N4: A1.GPIO15, MX_SOCKET1.pin2
  N5: A1.GPIO7, R3.Pin_1
  N6: A1.ID_SC, R4.Pin_1
  N7: A1.GPIO12, LED2.cathode, LED3.cathode, LED4.cathode, LED5.cathode
  N8: LED2.anode, R1.Pin_0
  N9: LED3.anode, R3.Pin_0
  N10: LED4.anode, R2.Pin_0
  N11: LED5.anode, R4.Pin_0

notes:
  220 Ohm
  P
  CO
  Reply-Forecast
  Consume
  Accept
  Produce/Reply
  Request Forecast
  Accounting

custom parts:
  Raspberry Pi 5: The RPi5, a faster version of the awesome Raspberry Pi4B ARM Board with 40 pin gpio.
  Kailh switch socket: Kailh switch socket for MX series key switches.
